# Fritzing sketch breadboard (saved by Fritzing 0.8.3b)
breadboards: 1

parts:
  LCD1 = LCD screen
  Part1 = Arduino Uno (Rev3)
  R1 = Resistor [tolerance=±5% resistance=330 package=THT]
  R2 = Resistor [tolerance=±5% resistance=330 package=THT]
  LED2 = LED - 5mm [color="Green (555nm)" package="5 mm [THT]"]
  LED1 = LED - 5mm [color="Red (633nm)" package="5 mm [THT]"]

nets:
  VSS: LCD1.VSS, LCD1.R/W, Part1.GND, R1.Pin_1, R2.Pin_1
  VDD: LCD1.VDD, LCD1.LED+, Part1.5V
  N1: LCD1.V0, Part1.D9_PWM
  N2: LCD1.RS, Part1.D12/MISO
  N3: LCD1.E, Part1.D11_PWM/MOSI
  N4: LCD1.DB4, Part1.D2
  N5: LCD1.DB5, Part1.D3_PWM
  N6: LCD1.DB6, Part1.D4
  N7: LCD1.DB7, Part1.D5_PWM
  N8: LCD1.LED-, R1.Pin_0
  N9: Part1.D6_PWM, LED2.anode
  N10: Part1.D7, LED1.anode
  N11: R2.Pin_0, LED2.cathode, LED1.cathode
